# Fritzing sketch Sketchv1 (saved by Fritzing 0.9.3b)
breadboards: 1

parts:
  Composant1 = Arduino Uno (Rev3) - ICSP
  M1 = DC Motor
  D1 = Rectifier Diode [part_number=1N4001 package="300 mil [THT]"]
  Q1 = pnp-Powertransistor [package="TO220 [THT]"]
  VCC1 = Battery block 9V
  hc-sr1 = hc-sr04
  Composant2 = Thumb Joystick

nets:
  N1: Composant1.A0, Composant2.VERT
  N2: Composant1.A1, Composant2.HORZ
  N3: Composant1.A2, Composant2.SEL
  N4: Composant1.ICSP_MOSI, Composant1.D11_PWM/MOSI, hc-sr1.Echo
  N5: Composant1.D9_PWM, Q1.base
  N6: Composant1.D10_PWM/SS, hc-sr1.Trig
  VCC: Composant1.5V, hc-sr1.VCC, Composant2.VCC
  GND: Composant1.GND, Q1.emitter, VCC1.-, hc-sr1.GND, Composant2.GND
  N7: M1.pin_1, D1.cathode, VCC1.+
  N8: M1.pin_2, D1.anode, Q1.collector
